# Fritzing sketch SmartMailBox_schema (saved by Fritzing 0.7.12b)
breadboards: 1

parts:
  Nano1 = Arduino Nano v2.3
  RFM12b1 = RFM12b HopeRF Transceiver
  S1 = Pushbutton [package="[SMD]"]
  R1 = 10k Ω Resistor [package=THT]
  LED1 = LED - 3mm [color="Red (633nm)" package="3 mm [THT]"]
  R2 = Resistor [tolerance=±5% resistance=220 package="0805 [SMD]"]
  PIR1 = PIR sensor

nets:
  GND: Nano1.GND, RFM12b1.10_GND, R1.Pin_1, LED1.cathode, PIR1.GND
  N1: Nano1.D2, RFM12b1.2_nIRQ
  N2: Nano1.D3, S1.Pin_3, S1.Pin_4, R1.Pin_0
  N3: Nano1.D5, R2.Pin_1
  N4: Nano1.D7, PIR1.SIG
  N5: Nano1.D10, RFM12b1.14_nSEL
  N6: Nano1.D11, RFM12b1.12_SDI
  N7: Nano1.D12, RFM12b1.1_SDO
  N8: Nano1.D13, RFM12b1.13_SCK
  N9: Nano1.3V3, RFM12b1.9_VDD
  +5V: Nano1.+5V, S1.Pin_1, S1.Pin_2, PIR1.VDD
  N10: LED1.anode, R2.Pin_0
